# Fritzing sketch tinkerAccess-Hat (saved by Fritzing 0.9.3b)
circuit board: 8.53488cm x 5.63626cm

parts:
  J1 = double row female pin header, 40 pins [form="♀ (female)"]
  S1_Logout = Momentary Switch [package=tactile-pth]
  U1 = RELAY [package=relay-g5q]
  LED1 = RGB LED (com. cathode, rgb) [package="5 mm [THT]"]
  R1 = Resistor [tolerance=±5% resistance=330 package=THT]
  R2 = Resistor [tolerance=±5% resistance=150 package=THT]
  R3 = Resistor [tolerance=±5% resistance=300 package=THT]
  R4 = Resistor [tolerance=±5% resistance=1k package=THT]
  J3 = female pin header, 2 pins [form="♀ (female)"]
  R5 = Resistor [tolerance=±5% resistance=1k package=THT]
  R6 = Resistor [tolerance=±5% resistance=1k package=THT]
  R7 = Resistor [tolerance=±5% resistance=1k package=THT]
  R8 = Resistor [tolerance=±5% resistance=1k package=THT]
  D1 = Rectifier Diode [part_number=1N4001 package="300 mil [THT]"]
  D2 = Rectifier Diode [part_number=1N4001 package="300 mil [THT]"]
  D3 = Rectifier Diode [part_number=1N4001 package="300 mil [THT]"]
  D4 = Rectifier Diode [part_number=1N4001 package="300 mil [THT]"]
  U2 = LM393 [package=so08]
  R9 = Resistor [tolerance=±5% resistance=1M package=THT]
  D5 = Rectifier Diode [part_number=1N4001 package="300 mil [THT]"]
  C1 = Electrolytic Capacitor [capacitance=1µF package="100 mil [THT, electrolytic]"]
  PCB1 = Raspberry Pi Shield [width=85.348826 height=56.36259999999999]  # not connected
  J2 = female pin header, 4 pins [form="♀ (female)"]

nets:
  N1: J1.pin1, J1.pin2, R7.Pin_0, R8.Pin_0, U2.G1_V+, J2.pin2
  GND: J1.pin3, J1.pin7, J1.pin10, J1.pin15, J1.pin17, J1.pin21, J1.pin28, J1.pin36, U1.COIL2, LED1.common_cathode, R5.Pin_1, R6.Pin_1, U2.G1_V-, U2.G2_+IN, U2.G2_-IN, R9.Pin_1, C1.-, J2.pin1
  N2: J1.pin16, R9.Pin_0, D5.cathode, C1.+
  N3: J1.pin18, S1_Logout.3, S1_Logout.4
  N4: J1.pin19, R3.Pin_0
  N5: J1.pin20, R1.Pin_0
  N6: J1.pin23, R2.Pin_0
  N7: J1.pin35, U1.COIL1
  N8: J1.pin38, J2.pin4
  N9: J1.pin39, J2.pin3
  N10: J1.pin40, S1_Logout.1, S1_Logout.2
  N11: LED1.red_anode, R1.Pin_1
  N12: LED1.green_anode, R2.Pin_1
  N13: LED1.blue_anode, R3.Pin_1
  N14: R4.Pin_0, J3.pin1, D1.anode, D3.cathode
  N15: R4.Pin_1, J3.pin2, D2.anode, D4.cathode
  N16: R5.Pin_0, R7.Pin_1, D3.anode, D4.anode, U2.G1_-IN
  N17: R6.Pin_0, D1.cathode, D2.cathode, U2.G1_+IN
  N18: R8.Pin_1, U2.G1_OUT, D5.anode

notes:
  tinkerAccess, tinkerAccess Hat designed by Chris Lindbergh with help from Tyler Dow, 1.0
  tinkerAccess Hat
  Load Relay
  Current
  Sense
  Coil
  I2C LCD Panel
  40-pin Header to Raspberry Pi
  4-pin Header to
  Load Control Relay
  Current Sense Coil
  2-pin Header to
  (NOTE: These pin numbers do not follow the same notation as the Raspberry Pi)
  5V
  GND
  GPIO7
  GPIO16
  GPIO12
  GPIO20
  GPIO21
  GPIO19
  GPIO14
  GPIO15
  GPIO18
  GPIO23
  GPIO24
  GPIO25
  GPIO8
  ID_SC
  GPIO26
  GPIO5
  GPIO13
  GPIO6
  GPIO27
  GPIO10
  GPIO4
  GPIO2
  GPIO22
  GPIO11
  3V3
  GPIO9
  GPIO17
  GPIO3
  ID_SD
  SDA
  SCL
  Normally Closed
  Normally Open
  Common
  AC In A
  AC In B

custom parts:
  Raspberry Pi Shield: Plain PCB Shaped to fit as Raspberry Pi B+ Hat
