# Fritzing sketch tinkerAccess (saved by Fritzing 0.9.3b)
breadboards: 1

parts:
  Raspberry_Pi_1 = Raspberry Pi 3 [part_number=RPI-3-V1.2]
  I2C_LCD = LCD1602-I2C
  S1_Reset = Round Pushbutton
  U1_Load_Relay = RELAY [package=relay-t9a-2]
  LED1 = RGB LED (com. cathode, rgb) [package="5 mm [THT]"]
  R1 = Resistor [tolerance=±5% resistance=330 package="0402 [SMD]"]
  R2 = Resistor [tolerance=±5% resistance=150 package="0402 [SMD]"]
  R3 = Resistor [tolerance=±5% resistance=300 package="0402 [SMD]"]
  U2_LM393 = LM393 [package=so08]
  D1 = Rectifier Diode [part_number=1N4001 package="300 mil [THT]"]
  D2 = Rectifier Diode [part_number=1N4001 package="300 mil [THT]"]
  D3 = Rectifier Diode [part_number=1N4001 package="300 mil [THT]"]
  D4 = Rectifier Diode [part_number=1N4001 package="300 mil [THT]"]
  D5 = Rectifier Diode [part_number=1N4001 package="300 mil [THT]"]
  L1_Current_Sense_Coil = Inductor [package="400 mil [THT]"]
  R4 = Resistor [tolerance=±5% resistance=1k package="0402 [SMD]"]
  R5 = Resistor [tolerance=±5% resistance=1k package="0402 [SMD]"]
  R6 = Resistor [tolerance=±5% resistance=1k package="0402 [SMD]"]
  R7 = Resistor [tolerance=±5% resistance=1k package="0402 [SMD]"]
  R8 = Resistor [tolerance=±5% resistance=1k package="0402 [SMD]"]
  R9 = Resistor [tolerance=±5% resistance=1M package="0402 [SMD]"]
  C1 = Ceramic Capacitor [capacitance=1µF package="1206 [SMD, multilayer]"]

nets:
  N1: Raspberry_Pi_1.3v3, S1_Reset.leg0
  N2: Raspberry_Pi_1.GPIO2, I2C_LCD.SDA
  N3: Raspberry_Pi_1.GPIO3, I2C_LCD.SCL
  N4: Raspberry_Pi_1.GIPO17, U1_Load_Relay.COIL1
  GND: Raspberry_Pi_1.GND, I2C_LCD.GND, U1_Load_Relay.COIL2, LED1.common_cathode, U2_LM393.G1_V-, U2_LM393.G2_+IN, U2_LM393.G2_-IN, R5.Pin_0, R6.Pin_0, R9.Pin_0, C1.0
  N5: Raspberry_Pi_1.GIPO19, R2.Pin_0
  N6: Raspberry_Pi_1.GIPO21, R1.Pin_0
  N7: Raspberry_Pi_1.GIPO20, R3.Pin_0
  N8: Raspberry_Pi_1.GIPO16, S1_Reset.leg1
  N9: Raspberry_Pi_1.GIPO12, D5.cathode, R9.Pin_1, C1.1
  5V: Raspberry_Pi_1.5V, I2C_LCD.VCC, U2_LM393.G1_V+, R7.Pin_1, R8.Pin_1
  N10: LED1.red_anode, R1.Pin_1
  N11: LED1.green_anode, R2.Pin_1
  N12: LED1.blue_anode, R3.Pin_1
  N13: U2_LM393.G1_OUT, D5.anode, R8.Pin_0
  N14: U2_LM393.G1_-IN, D3.anode, D4.anode, R5.Pin_1, R7.Pin_0
  N15: U2_LM393.G1_+IN, D1.cathode, D2.cathode, R6.Pin_1
  N16: D1.anode, D3.cathode, L1_Current_Sense_Coil.pin_0, R4.Pin_1
  N17: D2.anode, D4.cathode, L1_Current_Sense_Coil.pin_1, R4.Pin_0

custom parts:
  LCD1602-I2C: A standard character display, usually with 2x16 characters. Comes in many colors with LCM1602 IIC attached.
